# Fritzing sketch multi-mcp23017 (saved by Fritzing 0.7.11b)
stripboards: 1

parts:
  RPi_GPIO1 = RPi GPIO Header [form="♂ (shrouded male)" package=THT]
  IC1 = MCP23017 I2C I/O Expander
  C1 = Ceramic Capacitor [capacitance=100nF voltage=20V package="100 mil [THT, multilayer]"]  # not connected
  J3 = male pin header, 3 pins [form="♂ (male)"]
  IC2 = MCP23017 I2C I/O Expander
  IC3 = MCP23017 I2C I/O Expander
  C2 = Ceramic Capacitor [capacitance=100nF voltage=20V package="100 mil [THT, multilayer]"]
  C3 = Ceramic Capacitor [capacitance=100nF voltage=20V package="100 mil [THT, multilayer]"]
  J2 = female pin header, 10 pins [form="♀ (female)"]
  J5 = female pin header, 10 pins [form="♀ (female)"]
  J7 = female pin header, 10 pins [form="♀ (female)"]
  JACK1 = 2.1mm DC Barrel Jack
  R1 = Resistor [tolerance=±5% resistance=10k package=THT]
  R2 = Resistor [tolerance=±5% resistance=10k package=THT]
  R3 = Resistor [tolerance=±5% resistance=10k package=THT]
  R4 = Resistor [tolerance=±5% resistance=10k package=THT]
  Q1 = NPN-Transistor [part_number=2N7000 package="TO92 [THT]"]
  Q2 = NPN-Transistor [part_number=2N7000 package="TO92 [THT]"]
  J1 = female pin header, 10 pins [form="♀ (female)"]
  J4 = female pin header, 10 pins [form="♀ (female)"]
  J6 = female pin header, 10 pins [form="♀ (female)"]

nets:
  N1: RPi_GPIO1.+3.3V, J3.pin3, R1.Pin_0, R2.Pin_0, Q1.B, Q2.B
  N2: RPi_GPIO1.GPIO_0_(SDA), R1.Pin_1, Q1.E
  VSS: RPi_GPIO1.Ground, IC1.VSS, IC1.A0, IC2.VSS, IC3.VSS, C2.1, C3.1, JACK1.sleeve, J1.pin10, J4.pin10, J6.pin10
  N3: RPi_GPIO1.+5V, J3.pin1
  N4: IC1.GPB0, J1.pin1
  N5: IC1.GPB1, J1.pin2
  N6: IC1.GPB2, J1.pin3
  N7: IC1.GPB3, J1.pin4
  N8: IC1.GPB4, J1.pin5
  N9: IC1.GPB5, J1.pin6
  N10: IC1.GPB6, J1.pin7
  N11: IC1.GPB7, J1.pin8
  VDD: IC1.VDD, IC1.RESET, J3.pin2, IC2.VDD, IC2.RESET, IC3.VDD, IC3.RESET, C2.0, C3.0, JACK1.switch, R3.Pin_1, R4.Pin_1, J1.pin9, J4.pin9, J6.pin9
  N12: IC1.SCL, IC2.SCL, IC3.SCL, R4.Pin_0, Q2.C
  N13: IC1.SDA, IC2.SDA, IC3.SDA, R3.Pin_0, Q1.C
  N14: IC1.INTB, J2.pin10
  N15: IC1.INTA, J2.pin9
  N16: IC1.GPA0, J2.pin8
  N17: IC1.GPA1, J2.pin7
  N18: IC1.GPA2, J2.pin6
  N19: IC1.GPA3, J2.pin5
  N20: IC1.GPA4, J2.pin4
  N21: IC1.GPA5, J2.pin3
  N22: IC1.GPA6, J2.pin2
  N23: IC1.GPA7, J2.pin1
  N24: IC2.GPB0, J4.pin1
  N25: IC2.GPB1, J4.pin2
  N26: IC2.GPB2, J4.pin3
  N27: IC2.GPB3, J4.pin4
  N28: IC2.GPB4, J4.pin5
  N29: IC2.GPB5, J4.pin6
  N30: IC2.GPB6, J4.pin7
  N31: IC2.GPB7, J4.pin8
  N32: IC2.INTB, J5.pin10
  N33: IC2.INTA, J5.pin9
  N34: IC2.GPA0, J5.pin8
  N35: IC2.GPA1, J5.pin7
  N36: IC2.GPA2, J5.pin6
  N37: IC2.GPA3, J5.pin5
  N38: IC2.GPA4, J5.pin4
  N39: IC2.GPA5, J5.pin3
  N40: IC2.GPA6, J5.pin2
  N41: IC2.GPA7, J5.pin1
  N42: IC3.GPB0, J6.pin1
  N43: IC3.GPB1, J6.pin2
  N44: IC3.GPB2, J6.pin3
  N45: IC3.GPB3, J6.pin4
  N46: IC3.GPB4, J6.pin5
  N47: IC3.GPB5, J6.pin6
  N48: IC3.GPB6, J6.pin7
  N49: IC3.GPB7, J6.pin8
  N50: IC3.INTB, J7.pin10
  N51: IC3.INTA, J7.pin9
  N52: IC3.GPA0, J7.pin8
  N53: IC3.GPA1, J7.pin7
  N54: IC3.GPA2, J7.pin6
  N55: IC3.GPA3, J7.pin5
  N56: IC3.GPA4, J7.pin4
  N57: IC3.GPA5, J7.pin3
  N58: IC3.GPA6, J7.pin2
  N59: IC3.GPA7, J7.pin1
  N60: R2.Pin_1, Q2.E

custom parts:
  MCP23017 I2C I/O Expander: MCP23017 I2C 16-Channel I/O Expander
  2.1mm DC Barrel Jack: 2.1mm DC Barrel Jack with Thru-Hole Connectors (breadboardable)
